# Fritzing sketch btfm (saved by Fritzing 1.0.2b)

parts:
  R1 = Resistor [tolerance=±5% resistance=68k power=0.25W package=THT]
  R2 = Resistor [tolerance=±5% resistance=18k power=0.25W package=THT]
  Part8 = Arduino Mega 2560 (Rev3)
  Si4713 = Si4713 Stereo FM Transmitter
  CMD_MODE = SWITCH_SPDT [package=kps-1290]
  RESET = Momentary Switch [package=ksa_sealed_tac_switch]
  NEXT = Momentary Switch [package=ksa_sealed_tac_switch]
  PLAY = Momentary Switch [package=ksa_sealed_tac_switch]
  PREV = Momentary Switch [package=ksa_sealed_tac_switch]
  POWER = Momentary Switch [package=ksa_sealed_tac_switch]
  VOL_UP = Momentary Switch [package=ksa_sealed_tac_switch]
  VOL_DN = Momentary Switch [package=ksa_sealed_tac_switch]
  C1 = Capacitor Polarized [mn="10 uF" mpn=25V package=cpol-radial-10uf-25v]
  C2 = Capacitor Polarized [mpn=25V mn=10uF package=cpol-radial-10uf-25v]
  FTDI_Breakout = SparkFun FTDI Basic Breakout - 3.3V [part_number=DEV-09873]
  R4 = Resistor [tolerance=±5% resistance=18k power=0.25W package=THT]
  R3 = Resistor [tolerance=±5% resistance=68k power=0.25W package=THT]
  RN-52_Breakout1 = RN-52 Breakout
  Part14 = Adafruit 2.8 inch Captouch TFT [part_number="Adafruit #2090"]
  J1 = female pin header, 2 pins [form="♀ (female)"]
  J2 = female pin header, 2 pins [form="♀ (female)"]
  J3 = female pin header, 2 pins [form="♀ (female)"]
  J4 = female pin header, 2 pins [form="♀ (female)"]
  J6 = female pin header, 7 pins [form="♀ (female)"]
  Right_Side_RN-52_Daughterboard = Adafruit_PermaProto_1_2_Board  # not connected
  Left_Side_RN-52_Daughterboard = Adafruit_PermaProto_1_2_Board  # not connected
  Si7413_Daughter_Board = adafruit  # not connected
  J5 = female pin header, 1 pin [form="♀ (female)"]
  J9 = female pin header, 20 pins [form="♀ (female)"]
  J10 = female pin header, 20 pins [form="♀ (female)"]
  J11 = female pin header, 11 pins [form="♀ (female)"]
  22_AWG = Antenna [mn=Planar mpn="16 cm square"]  # not connected
  SWD_to_JTAG_pins = Adafruit 2x5 SWD Breakout [part_number="Adafruit #2743"]
  ISCP = Adafruit AVR 6-ISP Breakout [part_number="Adafruit #1465"]
  J7 = female pin header, 11 pins [form="♀ (female)"]
  C3 = Ceramic Capacitor [capacitance=0.47µF voltage=35V package="100 mil [THT, multilayer]"]
  C4 = Ceramic Capacitor [capacitance=0.47µF voltage=35V package="100 mil [THT, multilayer]"]
  L1 = Inductor [mn="Q > 40" inductance=120nH package="400 mil [THT]"]
  Part16 = Adafruit Micro USB Breakout [part_number="Adafruit #1833"]  # not connected
  Level_Shifter = I2C level shifter bidirectional
  C5 = Capacitor Polarized [mpn=25V mn=10uF package=cpol-radial-10uf-25v]
  PROG/DEBUG_MODE_SWITCH = Toggle Switch [package=THT]

nets (from the schematic view):
  J2 GND/J4 GND/J9 GND/MEGA GND/RN-52 GND/Si4713 ANT/Si4713 GND: R1.Pin_0, Part8.GND, Si4713.ANT, Si4713.GND, VOL_UP.1, VOL_DN.1, C1.-, C2.-, R3.Pin_0, RN-52_Breakout1.GND, Part14.GND, J2.pin2, J4.pin1, J5.pin1, J9.pin20, J11.pin9, SWD_to_JTAG_pins.SWIO, SWD_to_JTAG_pins.RESET, ISCP.GND, J7.pin9, L1.pin_0, L1.pin_1, Level_Shifter.GND, C5.-
  J1 LIN/Si4713 LIN: R1.Pin_1, R2.Pin_1, J1.pin2, J11.pin10, J7.pin10, C4.1
  J8 SPK_L+: R2.Pin_0, C1.+
  JTAG TCK: Part8.A4, SWD_to_JTAG_pins.VREF
  JTAG TMS: Part8.A5, SWD_to_JTAG_pins.GND2
  JTAG TDO: Part8.A6, SWD_to_JTAG_pins.GND
  JTAG TDI: Part8.A7, SWD_to_JTAG_pins.GNDD
  MEGA SCL/Si4713 SCL: Part8.D21/SCL, Part8.SCL, Si4713.SCL, Part14.SCL, J6.pin3, J11.pin3, J7.pin3, Level_Shifter.LV3, Level_Shifter.HV3
  MEGA SDA/Si4713 SDA: Part8.D20/SDA, Part8.SDA, Si4713.SDA, Part14.SDA, J6.pin4, J11.pin4, J7.pin4, Level_Shifter.LV4, Level_Shifter.HV4
  TFT CS: Part8.D10_PWM, Part14.CS
  TFT DC: Part8.D9_PWM, Part14.D/C_WR
  MEGA RESET: Part8.RESET, SWD_to_JTAG_pins.SWO, SWD_to_JTAG_pins.NC, ISCP.RST, PROG/DEBUG_MODE_SWITCH.COM
  J3 3.3+V/J4 3.3+V/MEGA 3.3+V/RN-52 3.3+V/Si4713 3.3+V: Part8.3V3, Si4713.+3V3, POWER.1, RN-52_Breakout1.3.3V, J2.pin1, J3.pin2, J10.pin20, J11.pin8, J7.pin8, Level_Shifter.LV
  MEGA 5+V: Part8.5V, Part14.VIN, SWD_to_JTAG_pins.CLK, ISCP.VCC, Level_Shifter.HV
  MEGA D4: Part8.D4_PWM, Part14.SD_CS
  MEGA D22/Si4713 RST: Part8.D22, Si4713.RST, J6.pin1, J11.pin1, J7.pin1, Level_Shifter.LV1, Level_Shifter.HV1
  ICSP MISO: Part8.D50, Part14.MISO, ISCP.MISO
  ICSP MOSI: Part8.D51, Part14.MOSI, ISCP.MOSI
  ICSP SCK: Part8.D52, Part14.C/D_CLK, ISCP.SCK
  N1: Si4713.RIN, C3.0
  N2: Si4713.LIN, C4.0
  GPIO9/MODE: CMD_MODE.O, RN-52_Breakout1.GPIO9, J10.pin10
  J3 GND: CMD_MODE.S, RESET.1, NEXT.1, PLAY.1, PREV.1, FTDI_Breakout.GND, J3.pin1
  GPIO4/Reset: RESET.3, RN-52_Breakout1.GPIO4, J10.pin4
  GPIO12/Next: NEXT.3, RN-52_Breakout1.GPIO12, J10.pin6
  GPIO13/Play: PLAY.3, RN-52_Breakout1.GPIO13, J10.pin7
  GPIO11/Prev: PREV.3, RN-52_Breakout1.GPIO11, J10.pin8
  PWR_EN/Power: POWER.3, RN-52_Breakout1.PWREN, J10.pin19
  GPIO10/GPIO5/Vol Up: VOL_UP.3, RN-52_Breakout1.GPIO10, RN-52_Breakout1.GPIO5, J10.pin5, J10.pin9
  Vol Dn: VOL_DN.3
  J8 SPK_R+: C2.+, R4.Pin_0
  FTDI RX/UART RX: FTDI_Breakout.RXI, RN-52_Breakout1.UART_TX, J10.pin16
  FTDI TX/UART TX: FTDI_Breakout.TXO, RN-52_Breakout1.UART_RX, J10.pin15
  J1 RIN/Si4713 RIN: R4.Pin_1, R3.Pin_1, J1.pin1, J11.pin11, J7.pin11, C3.1
  SPK_L+: RN-52_Breakout1.SPKR_L+, J9.pin1
  SPK_R+: RN-52_Breakout1.SPKR_R+, J9.pin2
  N3: J6.pin2, J11.pin2
  N4: J6.pin5, J11.pin5, J7.pin5
  N5: J6.pin6, J11.pin6, J7.pin6
  N6: J6.pin7, J11.pin7, J7.pin7
  N7: C5.+, PROG/DEBUG_MODE_SWITCH.L2

notes:
  BTFM, Sparkfun RN-52 Bluetooth Shield to Si4713 FM Transmitter, 2
  Speaker Level Attenuator to Line Level
  ICSP Programming Shield
  SWD to JTAG Debugging Shield
  750 mV vPk
  636 mV max on each

custom parts:
  Si4713 Stereo FM Transmitter: Yaaar! Become your very own pirate radio station with this FM radio transmitter. This breakout board, based on the best-of-class Si4713, is an all-in-one stereo audio FM transmitter that can also transmit RDS/RBDS data!
  SparkFun FTDI Basic Breakout - 3.3V: Description: This is the newest revision of our FTDI Basic. We now use a SMD 6-pin header on the bottom, which makes it smaller and more compact. Functionality has remained the same. This is a basic breakout board for the FTDI FT232RL USB to serial IC. The pinout of this board matches the FTDI cable to work with official Arduino and cloned 3.3V Arduino boards. It can also be used for general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
  Adafruit 2.8 inch Captouch TFT: Add some jazz & pizazz to your project with a color capactive touchscreen LCD. This TFT display is big (2.8" diagonal) bright (4 white-LED backlight) and colorful! 240x320 pixels with individual RGB pixel control, this has way more resolution than a black and white 128x64 display. As a bonus, this display has a capacitive single-touch touchscreen attached to it already, so you can detect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
  Adafruit 2x5 SWD Breakout: This adapter board is designed to make it easier to use ARM dev boards that use slimmer 2x5 (0.05"/1.27mm pitch) SWD cables for programming. It's helpful for using products like the JTAGulator, STLink or SEGGER J-Link with tiny boards that use the 10-pin SWD programming connector, often Cortex M0 or M3's. This board comes with no cables. It's really just the breakout board and some header if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
  Adafruit AVR 6-ISP Breakout: Programming AVR? Always Googling the pinout? Well, now no longer! It's rare to find a mini kit so elegant, it deserves its own Haiku. A simple breakout, 2x3 box header in the center, two 1x3's on the side. Plugs into any breadboard for neat wiring (in both nifty and clean senses of the word). Comes with a quality mini PCB, a 2x3 box header and a small stick of 0.1" header. Requires some light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
  Adafruit Micro USB Breakout: Simple but effective - this breakout board has a USB Micro-B connector, with all 5 pins broken out. Great for pairing with a microcontroller with USB support, or adding USB 5V power to a project. We use a micro-AB connector with through-hole shielding pads for an excellent strong connection - it won't rip off by accident! Comes with one fully assembled and tested micro B breakout PCB and a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
